# Fritzing sketch P.I_Fritzing (saved by Fritzing 0.9.5d)
breadboards: 2

parts:
  U1 = ESP8266 NodeMCU LoLin module
  U2 = ESP8266 NodeMCU LoLin module
  M1 = Osoyoo SX1278-ra-02
  M2 = Osoyoo SX1278-ra-02
  DHT1 = DHT11 Humitidy and Temperature Sensor (3 pins)
  R1 = Photocell (LDR) [package=THT]
  R2 = Resistor [tolerance=±5% resistance=220 package="2010 [SMD]"]

nets:
  N1: U1.D2, M2.DIO0
  N2: U1.D3, M2.RST
  GND: U1.GND, M2.GND
  N3: U1.D5, M2.SCK
  N4: U1.D6, M2.MISO
  N5: U1.D7, M2.MOSI
  N6: U1.D8, M2.NSS
  N7: U2.D1, DHT1.Signal
  N8: U2.D2, M1.DIO0
  N9: U2.D3, M1.RST
  3V3: U2.3V3, M1.3.3V, DHT1.Plus, R1.pin_0
  GND_2: U2.GND, M1.GND, DHT1.Gnd, R2.Pin_1
  N10: U2.D5, M1.SCK
  N11: U2.D6, M1.MISO
  N12: U2.D7, M1.MOSI
  N13: U2.D8, M1.NSS
  N14: U2.A0, R1.pin_1, R2.Pin_0

custom parts:
  ESP8266 NodeMCU LoLin module: ESP8266 based NodeMCU
  Osoyoo SX1278-ra-02: Osoyoo Long Distance wireless transceiver Uart LoRa Module.
  DHT11 Humitidy and Temperature Sensor (3 pins): DHT11 Humidity and Temperature Sensor (3 pins).
